# Fritzing sketch schematic (saved by Fritzing 0.8.7b)
breadboards: 1

parts:
  Arduino = Arduino Uno (Rev3)
  SR = 74HC595 [package="DIP16 [THT]"]
  R1 = Resistor [tolerance=±5% resistance=220 package=THT]
  R2 = Resistor [tolerance=±5% resistance=10k package=THT]
  R3 = Resistor [tolerance=±5% resistance=10k package=THT]
  R4 = Resistor [tolerance=±5% resistance=10k package=THT]
  R5 = Resistor [tolerance=±5% resistance=10k package=THT]
  R6 = Resistor [tolerance=±5% resistance=10k package=THT]
  R7 = Resistor [tolerance=±5% resistance=10k package=THT]
  R8 = Resistor [tolerance=±5% resistance=10k package=THT]
  R9 = Resistor [tolerance=±5% resistance=10k package=THT]
  R10 = Resistor [tolerance=±5% resistance=10k package=THT]
  POT1 = POT [package=pot_alpha_rv16af-20]
  POT2 = POT [package=pot_alpha_rv16af-20]
  POT3 = POT [package=pot_alpha_rv16af-20]
  R11 = Resistor [tolerance=±5% resistance=10k package=THT]
  R12 = Resistor [tolerance=±5% resistance=10k package=THT]
  R13 = Resistor [tolerance=±5% resistance=1k package=THT]
  R14 = Resistor [tolerance=±5% resistance=2.2k package=THT]
  R15 = Resistor [tolerance=±5% resistance=4.7k package=THT]
  R16 = Resistor [tolerance=±5% resistance=10k package=THT]
  R17 = Resistor [tolerance=±5% resistance=22k package=THT]
  R18 = Resistor [tolerance=±5% resistance=47k package=THT]
  R19 = Resistor [tolerance=±5% resistance=10k package=THT]
  R20 = Resistor [tolerance=±5% resistance=4.7k package=THT]
  R21 = Resistor [tolerance=±5% resistance=47k package=THT]
  R22 = Resistor [tolerance=±5% resistance=1k package=THT]
  R23 = Resistor [tolerance=±5% resistance=22k package=THT]
  R24 = Resistor [tolerance=±5% resistance=2.2k package=THT]
  MIDI_OUT = DIN-5 jack (MIDI) [package=THT]

nets:
  To Sleeve of Sustain Pedal TRS: Arduino.A0, R10.Pin_0
  N1: Arduino.A1, POT1.S
  N2: Arduino.A2, POT2.S
  N3: Arduino.A3, POT3.S
  Scan Matrix Row 7: Arduino.D8, R8.Pin_0
  Scan Matrix Row 8: Arduino.D9_PWM, R9.Pin_0
  N4: Arduino.D10_PWM/SS, SR.SH_CP
  N5: Arduino.D11_PWM/MOSI, SR.ST_CP
  N6: Arduino.D12/MISO, SR.DS
  GND: Arduino.GND, SR.GND, SR.OE, R2.Pin_1, R3.Pin_1, R4.Pin_1, R5.Pin_1, R6.Pin_1, R7.Pin_1, R8.Pin_1, R9.Pin_1, R10.Pin_1, POT1.A, POT2.A, POT3.A, R11.Pin_1, R12.Pin_1, MIDI_OUT.2, MIDI_OUT.GND
  N7: Arduino.A4/SDA, R12.Pin_0, R13.Pin_1, R14.Pin_1, R15.Pin_1, R16.Pin_1, R17.Pin_1, R18.Pin_1
  N8: Arduino.A5/SCL, R11.Pin_0, R19.Pin_1, R20.Pin_1, R21.Pin_1, R22.Pin_1, R23.Pin_1, R24.Pin_1
  N9: Arduino.D1/TX, MIDI_OUT.4
  Scan Matrix Row 1: Arduino.D2, R2.Pin_0
  Scan Matrix Row 2: Arduino.D3_PWM, R3.Pin_0
  Scan Matrix Row 3: Arduino.D4, R4.Pin_0
  Scan Matrix Row 4: Arduino.D5_PWM, R5.Pin_0
  Scan Matrix Row 5: Arduino.D6_PWM, R6.Pin_0
  Scan Matrix Row 6: Arduino.D7, R7.Pin_0
  To Tip of Sustain Pedal TRS: Arduino.5V, SR.MR, SR.VCC, R1.Pin_0, POT1.E, POT2.E, POT3.E
  Scan Matrix Column 1: SR.Q1
  Scan Matrix Column 2: SR.Q2
  Scan Matrix Column 3: SR.Q3
  Scan Matrix Column 4: SR.Q4
  Scan Matrix Column 5: SR.Q5
  Scan Matrix Column 6: SR.Q6
  Scan Matrix Column 7: SR.Q7
  N10: R1.Pin_1, MIDI_OUT.5
  Rotary Switch 1 Pos 6: R13.Pin_0, R22.Pin_0
  Rotary Switch 1 Pos 5: R14.Pin_0, R24.Pin_0
  Rotary Switch 1 Pos 4: R15.Pin_0, R20.Pin_0
  Rotary Switch 1 Pos 3: R16.Pin_0, R19.Pin_0
  Rotary Switch 1 Pos 2: R17.Pin_0, R23.Pin_0
  Rotary Switch 1 Pos 1: R18.Pin_0, R21.Pin_0
